# Fritzing sketch AudioBootloader (saved by Fritzing 0.9.3b)
breadboards: 1

parts:
  U1 = attiny85 [package=dip]
  C1 = Ceramic Capacitor [capacitance=100nF package="100 mil [THT, multilayer]"]
  C3 = Ceramic Capacitor [capacitance=100nF package="100 mil [THT, multilayer]"]
  TRS1 = Audio Jack (TRS) 3.5mm [package="4Ucon 08780 [THT]"]
  R4 = Resistor [tolerance=±5% resistance=10k package=THT]
  LED1 = LED - 5mm [color="Red (633nm)" package="5 mm [THT]"]
  R8 = Resistor [tolerance=±5% resistance=1k package=THT]
  R9 = Resistor [tolerance=±5% resistance=10k package=THT]

nets:
  N1: U1.Pin_2, C1.0, R4.Pin_0, R9.Pin_1
  GND: U1.Pin_4, C3.1, TRS1.Sleeve, R4.Pin_1, LED1.cathode
  N2: U1.Pin_6, R8.Pin_0
  VCC: U1.Pin_8, C3.0, R9.Pin_0
  N3: C1.1, TRS1.Ring
  N4: LED1.anode, R8.Pin_1

notes:
  SoundProgInput
  AudioBootloader breadboard
  LED is optional
